# Fritzing sketch PhysicalLedRingWebUSB (saved by Fritzing 0.9.3b)

parts:
  Componente1 = 16 NeoPixel Ring [part_number=1463]
  Componente3 = Arduino Micro (Rev3)

nets:
  N1: Componente1.IN, Componente3.D6_PWM/A7
  VDD: Componente1.VDD, Componente3.5V
  GND: Componente1.GND, Componente3.GND

notes:
  NeoPixel Ring with 16 Leds
  Pin D6
  VCC
  GND

custom parts:
  16 NeoPixel Ring: 16 ultra bright smart LED NeoPixels are arranged in a circle with 1.75" (44.5mm) outer diameter. The rings are 'chainable' - connect the output pin of one to the input pin of another. Use only one microcontroller pin to control as many as you can chain together! Each LED is addressable as the driver chip is inside the LED. Each one has ~18mA constant current drive so the color will be very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
